# Fritzing sketch Esq_LCD_LM35 (saved by Fritzing 0.9.3b)
breadboards: 1

parts:
  U1 = NodeMCU V1.0
  Display1 = LCD screen 16x2 IIC [part_number=101290]
  T1 = LM35 Temperature Sensor [package="TO92 [THT]"]

nets:
  N1: U1.D1, Display1.SCL
  N2: U1.D2, Display1.SDA
  N3: U1.A0, T1.Vout

custom parts:
  NodeMCU V1.0: ESP8266 based NodeMCU
  LCD screen 16x2 IIC: LCD screen with HD44780 controller enables showing text, symbols, value or anything else that comes from Croduino/Arduino. It is capable of showing 16 symbols in two lines and therefore can be used in many projects that need to send clearly visible and legible output information.. • Color of symbols: White • Backlight: Blue • Dimensions: 80 x 36 x 12 mm • Screen dimensions: 64.5 x 16 mm •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
